// Digital circuit baby8.dig as structural Verilog
module baby8 (
  input  reset,
  input  clock,
  input  interrupt
);

  wire IR_q;
  wire [5:0] registers_db_2;
  wire [7:0] add_1_s, and_1_out, main_memory_d, multiplexer_1_out, multiplexer_2_out, multiplexer_3_out,
       not_1_out, or_1_out, prevR_q, registers_db, xor_1_out;
  wire [15:0] registers_da;

  RegisterFile #(.AddrBits(4), .Bits(8)) registers (
    .Din(add_1_s), .C(clock), .Da(registers_da[15:8]), .Db({registers_db[7], registers_db_2, registers_db[0]}));  // open: we, Rw, Ra, Rb
  Multiplexer #(.Bits(8)) multiplexer_1 (
    .in_0({registers_db[7], registers_db_2, registers_db[0]}), .in_1(main_memory_d), .out(multiplexer_1_out));  // open: sel
  assign and_1_out = registers_da[15:8] & multiplexer_1_out;  // And and_1, 8 bits wide
  assign or_1_out = registers_da[15:8] | multiplexer_1_out;  // Or or_1, 8 bits wide
  assign xor_1_out = registers_da[15:8] ^ multiplexer_1_out;  // XOr xor_1, 8 bits wide
  assign not_1_out = ~registers_da[15:8];  // Not not_1, 8 bits wide
  Multiplexer #(.Bits(8), .Selector_Bits(2)) multiplexer_2 (
    .in_0(registers_da[15:8]), .in_1(not_1_out), .in_2({8{1'b0}}), .in_3(8'hfe), .out(multiplexer_2_out));  // open: sel
  Multiplexer #(.Bits(8), .Selector_Bits(2)) multiplexer_3 (
    .in_0(and_1_out), .in_1(or_1_out), .in_2(xor_1_out), .in_3(multiplexer_1_out), .out(multiplexer_3_out));  // open: sel
  Multiplexer multiplexer_4 (.in_0(registers_db[7]), .out(registers_da[7]));  // open: sel, in_1
  Multiplexer multiplexer_5 (.in_0(registers_db[0]), .out(registers_da[0]));  // open: sel, in_1
  Add #(.Bits(8)) add_1 (.a(multiplexer_2_out), .b(multiplexer_3_out), .s(add_1_s));  // open: c_i, c_o
  Register prevR (.D(add_1_s[0]), .C(clock), .Q(prevR_q[0]));  // open: en
  BlockRAMDualPort #(.AddrBits(12), .Bits(8)) main_memory (
    .A({registers_da[11:7], registers_db_2, registers_da[0]}), .Din(prevR_q), .C(clock), .D(main_memory_d));  // open: str
  Register IR (.D(main_memory_d[0]), .C(clock), .Q(IR_q));  // open: en
  // Pins of 1 and 8 bits meet at add_1_s
  // Pins of 1 and 8 bits meet at prevR_q
  // Pins of 1 and 8 bits meet at main_memory_d
endmodule
