// Digital circuit baby8_control.dig as structural Verilog
module baby8_control (
  input  [7:0] dIn,
  input  Z,
  input  C,
  input  N,
  input  V,
  input  clock,
  input  resetn,
  input  \int ,
  output wReg,
  output [3:0] wAd,
  output [3:0] aAd,
  output [3:0] bAd,
  output [1:0] bSel,
  output [1:0] logSel,
  output [1:0] aSel,
  output Cin,
  output A7,
  output A0,
  output a7S,
  output a0S,
  output wMem,
  output out3,
  output out2,
  output out1,
  output out0,
  output rMem
);

  wire and_1_out, and_2_out, and_3_out, curInt, decode_1_zd, decode_1_zs, imm, jump, k, math, nextFetch,
       prevK, svZD, svZInc, svZInd, svZIO, svZReg, svZS, test, useK, wFl, wIR, wZL;
  wire [1:0] svD, svS;
  wire [2:0] decode_1_aluop, jop, svAluOp;
  wire [3:0] decode_1_cond;

  and and_1 (and_1_out, dIn[2], dIn[3]);
  and and_2 (and_2_out, nextFetch, ~useK);  // And
  and and_3 (and_3_out, ~dIn[4], ~dIn[5], ~dIn[6]);  // And
  Register register_1 (.D(\int ), .C(clock), .en(and_2_out), .Q(curInt));
  Register register_2 (.D(dIn[7]), .C(clock), .en(wZL), .Q(svZInd));
  Register register_3 (.D(dIn[0]), .C(clock), .en(wZL), .Q(svZInc));
  Register register_4 (.D(and_1_out), .C(clock), .en(wZL), .Q(svZIO));
  Register register_5 (.D(and_3_out), .C(clock), .en(wZL), .Q(svZReg));
  decode decode_1 (
    .dIn(dIn), .test(test), .k(k), .zd(decode_1_zd), .zs(decode_1_zs), .math(math), .imm(imm), .jump(jump),
    .jop(jop), .aluOp(decode_1_aluop), .cond(decode_1_cond));
  test test_1 (
    .flags({V, N, C, Z}), .curInt(curInt), .clock(clock), .saveFlags(wFl), .cond(decode_1_cond));  // open: tr
  Register register_6 (.D(useK), .C(clock), .en(wIR), .Q(prevK));
  Register register_7 (.D(k), .C(clock), .en(wIR), .Q(useK));
  Register register_8 (.D(decode_1_zd), .C(clock), .en(wIR), .Q(svZD));
  Register register_9 (.D(decode_1_zs), .C(clock), .en(wIR), .Q(svZS));
  Register #(.Bits(3)) register_10 (.D(decode_1_aluop), .C(clock), .en(wIR), .Q(svAluOp));
  Register #(.Bits(2)) register_11 (.D(decode_1_cond[1:0]), .C(clock), .en(wIR), .Q(svD));
  Register #(.Bits(2)) register_12 (.D(decode_1_cond[3:2]), .C(clock), .en(wIR), .Q(svS));

  // Other names for the same wires on the sheet: ZInd = dIn[7]

  // Notes on the sheet:
  //   dIn: data from external memory
  //   Z: zero flag from ALU
  //   C: carry flag from ALU
  //   N: negative flag from ALU
  //   V: overflow flag from ALU
  //   clock: system clock
  //   resetn: resets system when low
  //   int: interrupt when high
  //   wReg: writes the selected register
  //   wAd: register to write
  //   aAd: register to read for second operand
  //   bAd: register to read for first operand
  //   bSel: use register, memory or i/o as operand
  //   logSel: logical operation
  //   aSel: normal, inverted or constant
  //   Cin: output carry in for ALU
  //   A7: replacement value for A7
  //   A0: replacement value for A0
  //   a7S: use alternative A7
  //   a0S: use alternative A0
  //   wMem: asks memory to save data
  //   out3: output port 3 should load dOut
  //   out2: output port 2 should load dOut
  //   out1: output port 1 should load dOut
  //   out0: output port 0 should load dOut
  //   rMem: asks memory to output data
endmodule
