// Digital circuit baby8_datapath.dig as structural Verilog
module baby8_datapath (
  input  clock,
  input  [7:0] in0,
  input  [7:0] in1,
  input  wReg,
  input  [3:0] wAd,
  input  [3:0] aAd,
  input  [3:0] bAd,
  input  [7:0] dIn,
  input  [1:0] bSel,
  input  [1:0] logSel,
  input  [1:0] aSel,
  input  Cin,
  input  A7,
  input  A0,
  input  a7S,
  input  a0S,
  output [7:0] R,
  output [7:0] dOut,
  output [15:0] address,
  output Z,
  output C,
  output N,
  output V
);

  wire and_2_out, and_3_out, or_3_out;
  wire [7:0] and_1_out, multiplexer_1_out, multiplexer_2_out, multiplexer_3_out, not_1_out, or_1_out,
       registers_db, xor_1_out;

  RegisterFile #(.AddrBits(4), .Bits(8)) registers (
    .Din({N, R[6:0]}), .we(wReg), .Rw(wAd), .C(clock), .Ra(aAd), .Rb(bAd), .Da(address[15:8]),
    .Db({registers_db[7], address[6:1], registers_db[0]}));
  Multiplexer #(.Selector_Bits(2), .Bits(8)) multiplexer_1 (
    .sel(bSel), .in_0({registers_db[7], address[6:1], registers_db[0]}), .in_1(dIn), .in_2(in0), .in_3(in1),
    .out(multiplexer_1_out));
  assign and_1_out = address[15:8] & multiplexer_1_out;  // And and_1, 8 bits wide
  assign or_1_out = address[15:8] | multiplexer_1_out;  // Or or_1, 8 bits wide
  assign xor_1_out = address[15:8] ^ multiplexer_1_out;  // XOr xor_1, 8 bits wide
  assign not_1_out = ~address[15:8];  // Not not_1, 8 bits wide
  Multiplexer #(.Selector_Bits(2), .Bits(8)) multiplexer_2 (
    .sel(aSel), .in_0(address[15:8]), .in_1(not_1_out), .in_2({8{1'b0}}), .in_3(8'hfe),
    .out(multiplexer_2_out));
  Multiplexer #(.Selector_Bits(2), .Bits(8)) multiplexer_3 (
    .sel(logSel), .in_0(and_1_out), .in_1(or_1_out), .in_2(xor_1_out), .in_3(multiplexer_1_out),
    .out(multiplexer_3_out));
  and and_2 (and_2_out, ~N, multiplexer_2_out[7], multiplexer_3_out[7]);  // And
  Multiplexer multiplexer_4 (.sel(a7S), .in_0(registers_db[7]), .in_1(A7), .out(address[7]));
  and and_3 (and_3_out, N, ~multiplexer_2_out[7], ~multiplexer_3_out[7]);  // And
  or or_2 (V, and_3_out, and_2_out);
  Multiplexer multiplexer_5 (.sel(a0S), .in_0(registers_db[0]), .in_1(A0), .out(address[0]));
  Add #(.Bits(8)) add_1 (.a(multiplexer_2_out), .b(multiplexer_3_out), .c_i(Cin), .s({N, R[6:0]}), .c_o(C));
  or or_3 (or_3_out, R[0], R[1], R[2], R[3], R[4], R[5], R[6], N);
  not not_2 (Z, or_3_out);
  Register #(.Bits(8)) prevR (.D({N, R[6:0]}), .C(clock), .en(1'b1), .Q(dOut));

  assign R[7] = N;
endmodule
