// Digital circuit test_term.dig as structural Verilog
module test_term (
  input  clk
);

  wire baby8cpu_1_p9, baby8cpu_1_p10, baby8cpu_1_p11, reset_1_out;
  wire [7:0] baby8cpu_1_p6, baby8cpu_1_p7;
  wire [9:0] baby8cpu_1_p8;

  Reset reset_1 (.out(reset_1_out));
  // baby8cpu baby8cpu_1: pin names not known; wires that end beside it: clk, reset_1_out, 1'b0, {8{1'b0}}, {8{1'b0}}, baby8cpu_1_p6, baby8cpu_1_p7, baby8cpu_1_p8, baby8cpu_1_p9, baby8cpu_1_p10, baby8cpu_1_p11
  RAMDualPort #(.AddrBits(10), .Bits(8)) _1KB (
    .A(baby8cpu_1_p8), .Din(baby8cpu_1_p7), .str(baby8cpu_1_p9), .C(clk), .ld(baby8cpu_1_p11),
    .D(baby8cpu_1_p6));
  Terminal terminal_1 (.D(baby8cpu_1_p7), .C(clk), .en(baby8cpu_1_p10));
endmodule
